# Fritzing sketch test_board (saved by Fritzing 0.9.3b)
breadboards: 1

parts:
  Grove1 = Grove OLED 128x96
  R2 = Photocell (LDR) [package=THT]
  부품1 = SRF05 Ultrasonic Rangefinder
  Raspberry_Pi_1 = Raspberry Pi 3 [part_number=RPI-3-V1.2]
  LED1 = LEDs [package=led10mm]
  LED2 = LEDs [package=led10mm]
  LED4 = LEDs [package=led10mm]
  R3 = Resistor [tolerance=±5% resistance=220 package=THT]
  R4 = Resistor [tolerance=±5% resistance=220 package=THT]
  R5 = Resistor [tolerance=±5% resistance=220 package=THT]
  C3 = Electrolytic Capacitor [capacitance=1µF package="100 mil [THT, electrolytic]"]

nets:
  GND: Grove1.GND, 부품1.GND, Raspberry_Pi_1.GND, LED1.C, LED2.C, LED4.C, C3.+
  VCC: Grove1.VCC, Raspberry_Pi_1.3v3
  N1: Grove1.SDA, Raspberry_Pi_1.GPIO2
  N2: Grove1.SCL, Raspberry_Pi_1.GPIO3
  VCC_2: R2.pin_0, 부품1.VCC, Raspberry_Pi_1.5V
  N3: R2.pin_1, Raspberry_Pi_1.GIPO4, C3.-
  N4: 부품1.Trig, Raspberry_Pi_1.GIPO21
  N5: 부품1.Echo, Raspberry_Pi_1.GIPO18
  N6: Raspberry_Pi_1.GIPO13, R4.Pin_0
  N7: Raspberry_Pi_1.GIPO19, R3.Pin_0
  N8: Raspberry_Pi_1.GIPO26, R5.Pin_0
  N9: LED1.A, R3.Pin_1
  N10: LED2.A, R4.Pin_1
  N11: LED4.A, R5.Pin_1
